# Fritzing sketch Aquaduino Sketch (saved by Fritzing 0.9.2b)
breadboards: 1

parts:
  Pro_Micro1 = Pro Micro  # not connected
  T1 = LM35 Temperature Sensor [package="TO92 [THT]"]
  R1 = Resistor [tolerance=±5% resistance=220 package=THT]
  U1 = Voltage Regulator - 5V [package="TO220 [THT]"]
  U2 = Voltage Regulator - 5V [package="TO220 [THT]"]
  U3 = Voltage Regulator - 5V [package="TO220 [THT]"]

nets:
  N1: T1.+Vs, R1.Pin_1, U1.input_voltage, U2.input_voltage, U3.input_voltage
  N2: T1.Vout, R1.Pin_0
  N3: T1.GND, U1.output_voltage, U2.output_voltage, U3.output_voltage

custom parts:
  Pro Micro: The SparkFun Pro Micro is a complete USB-based microcontoller development system, in a very small footprint, capable of implementing many types of projects. All programming can be done via the USB port.
